// Logisim project alu32.circ as structural Verilog: 1 circuit, main circuit main
module main (
  input  [31:0] A,
  input  [31:0] B,
  input  [2:0] in_3,
  output [31:0] out_4
);

  wire [4:0] b4;
  wire [31:0] and_1_out, or_1_out, shifter_1_out, shifter_2_out, shifter_3_out, shifter_4_out, shifter_5_out,
       xor_1_out;

  Bit_Extender #(.in_width(32), .out_width(5)) bit_extender_1 (.in(B), .out(b4));
  Shifter #(.width(32)) shifter_1 (.in(A), .\dist (b4), .out(shifter_1_out));
  Shifter #(.width(32), .shift("lr")) shifter_2 (.in(A), .\dist (b4), .out(shifter_2_out));
  Shifter #(.width(32), .shift("ar")) shifter_3 (.in(A), .\dist (b4), .out(shifter_3_out));
  Shifter #(.width(32), .shift("rl")) shifter_4 (.in(A), .\dist (b4), .out(shifter_4_out));
  Shifter #(.width(32), .shift("rr")) shifter_5 (.in(A), .\dist (b4), .out(shifter_5_out));
  assign and_1_out = A & B;  // AND_Gate and_1, 32 bits wide
  assign or_1_out = A | B;  // OR_Gate or_1, 32 bits wide
  assign xor_1_out = A ^ B;  // XOR_Gate xor_1, 32 bits wide
  Multiplexer #(.select(3), .width(32)) multiplexer_1 (
    .in0(shifter_1_out), .in1(shifter_2_out), .in2(shifter_3_out), .in3(shifter_4_out), .in4(shifter_5_out),
    .in5(and_1_out), .in6(or_1_out), .in7(xor_1_out), .out(out_4), .sel(in_3), .en(1'b1));
endmodule
