// Logisim project fib.circ as structural Verilog
module fib_gen (
);

  wire clock_1_out, comparator_1_gt, not_1_out, register_1_q;
  wire [11:0] adder_1_out, bit_extender_1_out, counter_1_q, multiplexer_1_out, register_2_q, register_3_q,
       register_4_q;

  assign bit_extender_1_out = {{11{1'b0}}, 1'b1};  // Bit_Extender bit_extender_1
  Register #(.width(1)) register_1 (.D(1'b1), .Q(register_1_q), .clk(clock_1_out));  // open: en, clr
  Multiplexer #(.width(12)) multiplexer_1 (
    .in0(bit_extender_1_out), .in1(register_4_q), .out(multiplexer_1_out), .sel(register_1_q));  // open: en
  Register #(.width(12)) register_2 (.D(adder_1_out), .Q(register_2_q), .clk(clock_1_out));  // open: en, clr
  Register #(.width(12)) register_3 (.D(multiplexer_1_out), .Q(register_3_q), .clk(clock_1_out));  // open: en, clr
  Clock clock_1 (.out(clock_1_out));
  Adder #(.width(12)) adder_1 (.a(register_2_q), .b(register_3_q), .out(adder_1_out));  // open: cin, cout
  Register #(.width(12)) register_4 (
    .D(adder_1_out), .en(not_1_out), .Q(register_4_q), .clk(clock_1_out));  // open: clr
  not not_1 (not_1_out, comparator_1_gt);
  // Probe on register_4_q
  Counter #(.width(12), .max('hfff)) counter_1 (
    .D(register_4_q), .Q(counter_1_q), .clk(clock_1_out));  // open: load, count, carry, clr
  // Probe on counter_1_q
  Comparator #(.width(12)) comparator_1 (.a(counter_1_q), .b(12'hf), .gt(comparator_1_gt));  // open: eq, lt
endmodule
