// Logisim project fsm0.circ as structural Verilog: 2 circuits, main circuit main
module main (
  output [1:0] PS,
  output out_2,
  output [1:0] NS,
  output [7:0] out_4
);

  wire clock_1_out, random_1_out;
  wire [7:0] adder_1_out, bit_extender_1_out;

  Random #(.width(1), .seed(45)) random_1 (.clk(clock_1_out), .out(random_1_out));  // open: next, clr
  cl cl_1 (.PS(PS), .Input(random_1_out), .NS(NS), .out(out_2));
  Register #(.width(2)) register_1 (.D(NS), .Q(PS), .clk(clock_1_out));  // open: en, clr
  Clock clock_1 (.out(clock_1_out));
  assign bit_extender_1_out = {{7{1'b0}}, out_2};  // Bit_Extender bit_extender_1
  Adder adder_1 (.a(bit_extender_1_out), .b(out_4), .out(adder_1_out));  // open: cin, cout
  Register register_2 (.D(adder_1_out), .Q(out_4), .clk(clock_1_out));  // open: en, clr
endmodule

module cl (
  input  [1:0] PS,
  input  Input,
  output [1:0] NS,
  output out
);

  wire [2:0] bit_extender_1_out, bit_extender_2_out, or_1_out, shifter_1_out;

  assign bit_extender_1_out = {{1{1'b0}}, PS};  // Bit_Extender bit_extender_1
  assign bit_extender_2_out = {{2{1'b0}}, Input};  // Bit_Extender bit_extender_2
  Shifter #(.width(3)) shifter_1 (.in(bit_extender_1_out), .\dist (2'b01), .out(shifter_1_out));
  assign or_1_out = shifter_1_out | bit_extender_2_out;  // OR_Gate or_1, 3 bits wide
  Multiplexer #(.select(3), .width(2)) multiplexer_1 (
    .in0(2'b00), .in1(2'b01), .in2(2'b00), .in3(2'b10), .in4(2'b00), .in5(2'b00), .out(NS), .sel(or_1_out));  // open: in6, in7, en
  Multiplexer #(.select(3)) multiplexer_2 (
    .in0(1'b0), .in1(1'b0), .in2(1'b0), .in3(1'b1), .in4(1'b1), .in5(1'b1), .out(out), .sel(or_1_out));  // open: in6, in7, en
endmodule
