// Logisim project pipelining.circ as structural Verilog: 1 circuit, main circuit main
module main (
  input  [15:0] in_1,
  input  [15:0] in_2,
  input  [15:0] in_3,
  input  [15:0] in_4
);

  wire t;
  wire [15:0] adder_1_out, adder_2_out, multiplier_1_out, multiplier_2_out, register_1_q, register_2_q,
       register_3_q;

  Clock clock_1 (.out(t));
  Multiplier #(.width(16)) multiplier_1 (.a(in_1), .b(in_2), .out(multiplier_1_out));  // open: cin, cout
  Multiplier #(.width(16)) multiplier_2 (.a(in_3), .b(in_4), .out(multiplier_2_out));  // open: cin, cout
  Register #(.width(16)) register_1 (.D(multiplier_2_out), .Q(register_1_q), .clk(t));  // open: en, clr
  Adder #(.width(16)) adder_1 (.a(multiplier_1_out), .b(register_2_q), .out(adder_1_out));  // open: cin, cout
  Adder #(.width(16)) adder_2 (.a(register_1_q), .b(register_3_q), .out(adder_2_out));  // open: cin, cout
  Register #(.width(16)) register_2 (.D(adder_1_out), .Q(register_2_q), .clk(t));  // open: en, clr
  Register #(.width(16)) register_3 (.D(adder_2_out), .Q(register_3_q), .clk(t));  // open: en, clr
  // Probe on register_2_q
  // Probe on register_3_q
endmodule
