// Logisim project alu.circ as structural Verilog: 8 circuits, main circuit main
module main (
  input  [31:0] X,
  input  [31:0] Y,
  input  [5:0] Switch__S,
  output Signed_Overflow,
  output [31:0] RESULT,
  output Equal
);

  wire comparator_1_lt, comparator_2_lt, comparator_3_eq;
  wire [4:0] x5, y5;
  wire [31:0] add, \and , and_1_out, bitpal, lfsr, \or , sll, slt, sltu, sra, srl, sub, x_high, x_low;

  Bit_Extender #(.in_width(32), .out_width(5)) bit_extender_1 (.in(X), .out(x5));
  Bit_Extender #(.in_width(32), .out_width(5)) bit_extender_2 (.in(Y), .out(y5));
  revbits revbits_1 (.in(X), .out(x_low));
  assign and_1_out = X & 32'hffff0000;  // AND_Gate and_1, 32 bits wide
  Adder #(.width(32)) adder_1 (.a(X), .b(Y), .out(add));  // open: cin, cout
  Subtractor #(.width(32)) subtractor_1 (.a(X), .b(Y), .out(sub));  // open: bin, bout
  Shifter #(.width(32)) shifter_1 (.in(X), .\dist (y5), .out(sll));
  Shifter #(.width(32), .shift("lr")) shifter_2 (.in(X), .\dist (y5), .out(srl));
  Shifter #(.width(32), .shift("ar")) shifter_3 (.in(X), .\dist (y5), .out(sra));
  Shifter #(.width(32), .shift("lr")) shifter_4 (.in(and_1_out), .\dist (5'b10000), .out(x_high));
  assign \and  = X & Y;  // AND_Gate and_2, 32 bits wide
  assign \or  = X | Y;  // OR_Gate or_1, 32 bits wide
  Comparator #(.width(32)) comparator_1 (.a(X), .b(Y), .lt(comparator_1_lt));  // open: gt, eq
  Comparator #(.width(32), .mode("unsigned")) comparator_2 (.a(X), .b(Y), .lt(comparator_2_lt));  // open: gt, eq
  Comparator #(.width(32), .mode("unsigned")) comparator_3 (
    .a(x_low), .b(x_high), .eq(comparator_3_eq));  // open: gt, lt
  AluMux u_bitpal (
    .sll(sll), .\or (\or ), .srl(srl), .slt(slt), .sra(sra), .sltu(sltu), .add(add), .bitpal(bitpal),
    .addu(add), .lfsr(lfsr), .sub(sub), .funct(Switch__S), .subu(sub), .\and (\and ), .out(RESULT));
  assign slt = {{31{1'b0}}, comparator_1_lt};  // Bit_Extender bit_extender_3
  assign sltu = {{31{1'b0}}, comparator_2_lt};  // Bit_Extender bit_extender_4
  assign bitpal = {{31{1'b0}}, comparator_3_eq};  // Bit_Extender bit_extender_5
  overflow overflow_1 (.x(X), .y(Y), .result(RESULT), .in_4(Switch__S), .out(Signed_Overflow));
  lfsr lfsr_1 (.x(X), .out(lfsr));
  Comparator #(.width(32)) comparator_4 (.a(X), .b(Y), .eq(Equal));  // open: gt, lt

  // Other names for the same wires on the sheet: s[5:0] = Switch__S

  // Notes on the sheet:
  //   INPUTS to your circuit
  //   INPUT to your circuit
  //   DON'T CHANGE THE INPUTS AND OUTPUTS! IF YOU DO SO, YOU NEED TO MAKE SURE THE PINS ARE IN THE RIGHT PLACES!
  //   OUTPUTS of your circuit
endmodule

module AluMux (
  input  [31:0] sll,
  input  [31:0] \or ,
  input  [31:0] srl,
  input  [31:0] slt,
  input  [31:0] sra,
  input  [31:0] sltu,
  input  [31:0] add,
  input  [31:0] bitpal,
  input  [31:0] addu,
  input  [31:0] lfsr,
  input  [31:0] sub,
  input  [5:0] funct,
  input  [31:0] subu,
  input  [31:0] \and ,
  output [31:0] out
);

  wire [31:0] choose_1_out, choose_2_out, choose_3_out, choose_4_out, choose_5_out, choose_6_out,
       choose_7_out, choose_8_out, choose_9_out, choose_10_out, choose_11_out, choose_12_out, choose_13_out;

  choose choose_1 (.\const (funct), .funct(6'b100101), .in(\or ), .out(choose_1_out));
  choose choose_2 (.\const (funct), .funct({6{1'b0}}), .in(sll), .out(choose_2_out));
  choose choose_3 (.\const (funct), .funct(6'b000010), .in(srl), .out(choose_3_out));
  choose choose_4 (.\const (funct), .funct(6'b000011), .in(sra), .out(choose_4_out));
  choose choose_5 (.\const (funct), .funct(6'b100000), .in(add), .out(choose_5_out));
  choose choose_6 (.\const (funct), .funct(6'b100001), .in(addu), .out(choose_6_out));
  choose choose_7 (.\const (funct), .funct(6'b100010), .in(sub), .out(choose_7_out));
  choose choose_8 (.\const (funct), .funct(6'b100011), .in(subu), .out(choose_8_out));
  choose choose_9 (.\const (funct), .funct(6'b100100), .in(\and ), .out(choose_9_out));
  assign out = choose_2_out | choose_3_out | choose_4_out | choose_5_out | choose_6_out | choose_7_out | choose_8_out | choose_9_out | choose_1_out | choose_13_out | choose_12_out | choose_11_out | choose_10_out;  // OR_Gate or_1, 32 bits wide
  choose choose_10 (.\const (funct), .funct(6'b101010), .in(slt), .out(choose_10_out));
  choose choose_11 (.\const (funct), .funct(6'b101011), .in(sltu), .out(choose_11_out));
  choose choose_12 (.\const (funct), .funct(6'b111110), .in(bitpal), .out(choose_12_out));
  choose choose_13 (.\const (funct), .funct({6{1'b1}}), .in(lfsr), .out(choose_13_out));
endmodule

module choose (
  input  [5:0] \const ,
  input  [5:0] funct,
  input  [31:0] in,
  output [31:0] out
);

  wire comparator_1_eq;

  Comparator #(.width(6)) comparator_1 (.a(\const ), .b(funct), .eq(comparator_1_eq));  // open: gt, lt
  Multiplexer #(.width(32)) multiplexer_1 (.in0({32{1'b0}}), .in1(in), .out(out), .sel(comparator_1_eq));  // open: en
endmodule

module temp (
);

  wire and_1_out, and_2_out, comparator_1_gt, comparator_2_lt, comparator_3_gt, comparator_4_lt,
       comparator_5_gt;
  wire [5:0] funct, subtractor_1_out, subtractor_2_out, subtractor_3_out;

  Comparator #(.width(6)) comparator_1 (.a(funct), .b(6'b011111), .gt(comparator_1_gt));  // open: eq, lt
  Comparator #(.width(6)) comparator_2 (.a(funct), .b(6'b100110), .lt(comparator_2_lt));  // open: gt, eq
  Comparator #(.width(6)) comparator_3 (.a(funct), .b(6'b101001), .gt(comparator_3_gt));  // open: eq, lt
  Comparator #(.width(6)) comparator_4 (.a(funct), .b(6'b101100), .lt(comparator_4_lt));  // open: gt, eq
  Comparator #(.width(6)) comparator_5 (.a(funct), .b(6'b111110), .gt(comparator_5_gt));  // open: eq, lt
  Subtractor #(.width(6)) subtractor_1 (.a(funct), .b(6'b011101), .out(subtractor_1_out));  // open: bin, bout
  and and_1 (and_1_out, comparator_1_gt, comparator_2_lt);
  and and_2 (and_2_out, comparator_3_gt, comparator_4_lt);
  Multiplexer #(.width(6)) multiplexer_1 (.in1(subtractor_1_out), .sel(and_1_out));  // open: in0, out, en
  Multiplexer #(.width(6)) multiplexer_2 (.in1(subtractor_2_out), .sel(and_2_out));  // open: in0, out, en
  Subtractor #(.width(6)) subtractor_2 (.a(funct), .b(6'b100001), .out(subtractor_2_out));  // open: bin, bout
  Subtractor #(.width(6)) subtractor_3 (.a(funct), .b(6'b110011), .out(subtractor_3_out));  // open: bin, bout
  Multiplexer #(.width(6)) multiplexer_3 (.in0(subtractor_3_out), .sel(comparator_5_gt));  // open: in1, out, en
endmodule

module overflow (
  input  [31:0] x,
  input  [31:0] y,
  input  [31:0] result,
  input  [5:0] in_4,
  output out
);

  wire add, and_3_out, and_4_out, and_5_out, and_6_out, inNeg, inPos, or_1_out, or_2_out, sub, sumNeg,
       sumPos, xNeg, xPos, yNeg, yPos;

  Comparator #(.width(32)) comparator_1 (.a(x), .b({32{1'b0}}), .gt(xPos), .lt(xNeg));  // open: eq
  Comparator #(.width(32)) comparator_2 (.a(y), .b({32{1'b0}}), .gt(yPos), .lt(yNeg));  // open: eq
  Comparator #(.width(32)) comparator_3 (.a(result), .b({32{1'b0}}), .gt(sumPos), .lt(sumNeg));  // open: eq
  Comparator #(.width(6), .mode("unsigned")) comparator_4 (.a(in_4), .b(6'b100000), .eq(add));  // open: gt, lt
  Comparator #(.width(6), .mode("unsigned")) comparator_5 (.a(in_4), .b(6'b100010), .eq(sub));  // open: gt, lt
  and and_1 (inPos, xPos, yPos);
  and and_2 (inNeg, xNeg, yNeg);
  and and_3 (and_3_out, inPos, add, sumNeg);
  and and_4 (and_4_out, inNeg, add, sumPos);
  and and_5 (and_5_out, xPos, sub, yNeg);
  and and_6 (and_6_out, xNeg, sub, yPos);
  or or_1 (or_1_out, and_3_out, and_4_out);
  or or_2 (or_2_out, and_5_out, and_6_out);
  or or_3 (out, or_2_out, or_1_out);
endmodule

module revbits (
  input  [31:0] in,
  output [31:0] out
);

  wire [31:0] _0, _1, _2, _3, _4, _5, _6, _7, _8, _9, _10, _11, _12, _13, _14, _15;

  bitselect bitselect_1 (.\bit (5'b01111), .in_1(in), .out(_0));
  bitselect bitselect_2 (.\bit (5'b00111), .in_1(in), .out(_8));
  bitselect bitselect_3 (.\bit (5'b01110), .in_1(in), .out(_1));
  bitselect bitselect_4 (.\bit (5'b00110), .in_1(in), .out(_9));
  assign out = _15 | _14 | _13 | _12 | _11 | _10 | _9 | _8 | _7 | _6 | _5 | _4 | _3 | _2 | _1 | _0;  // OR_Gate or_1, 32 bits wide
  bitselect bitselect_5 (.\bit (5'b01101), .in_1(in), .out(_2));
  bitselect bitselect_6 (.\bit (5'b00101), .in_1(in), .out(_10));
  bitselect bitselect_7 (.\bit (5'b11100), .in_1(in), .out(_3));
  bitselect bitselect_8 (.\bit (5'b00100), .in_1(in), .out(_11));
  bitselect bitselect_9 (.\bit (5'b01011), .in_1(in), .out(_4));
  bitselect bitselect_10 (.\bit (5'b00011), .in_1(in), .out(_12));
  bitselect bitselect_11 (.\bit (5'b01010), .in_1(in), .out(_5));
  bitselect bitselect_12 (.\bit (5'b00010), .in_1(in), .out(_13));
  bitselect bitselect_13 (.\bit (5'b01001), .in_1(in), .out(_6));
  bitselect bitselect_14 (.\bit (5'b00001), .in_1(in), .out(_14));
  bitselect bitselect_15 (.\bit (5'b01000), .in_1(in), .out(_7));
  bitselect bitselect_16 (.\bit ({5{1'b0}}), .in_1(in), .out(_15));

  // Other names for the same wires on the sheet: s[31:0] = in
endmodule

module bitselect (
  input  [31:0] in_1,
  input  [4:0] \bit ,
  output [31:0] out
);

  wire bitselector_1_out;
  wire [4:0] subtractor_1_out;
  wire [31:0] bit_extender_1_out;

  BitSelector #(.width(32)) bitselector_1 (.in(in_1), .out(bitselector_1_out), .sel(subtractor_1_out));
  assign bit_extender_1_out = {{31{1'b0}}, bitselector_1_out};  // Bit_Extender bit_extender_1
  Subtractor #(.width(5)) subtractor_1 (.a(5'b01111), .b(\bit ), .out(subtractor_1_out));  // open: bin, bout
  Shifter #(.width(32)) shifter_1 (.in(bit_extender_1_out), .\dist (\bit ), .out(out));
endmodule

module lfsr (
  input  [31:0] x,
  output [31:0] out
);

  wire bitselector_1_out, bitselector_2_out, bitselector_3_out, bitselector_4_out, xor_1_out;
  wire [31:0] bit_extender_1_out, shifter_1_out, shifter_2_out;

  BitSelector #(.width(32)) bitselector_1 (.in(x), .out(bitselector_1_out), .sel({5{1'b0}}));
  BitSelector #(.width(32)) bitselector_2 (.in(x), .out(bitselector_2_out), .sel(5'b00010));
  BitSelector #(.width(32)) bitselector_3 (.in(x), .out(bitselector_3_out), .sel(5'b00011));
  BitSelector #(.width(32)) bitselector_4 (.in(x), .out(bitselector_4_out), .sel(5'b00101));
  ExactlyOne xor_1 (
    .out(xor_1_out), .in0(bitselector_1_out), .in1(bitselector_2_out), .in2(bitselector_3_out),
    .in3(bitselector_4_out));
  assign bit_extender_1_out = {{31{1'b0}}, xor_1_out};  // Bit_Extender bit_extender_1
  Shifter #(.width(32)) shifter_1 (.in(bit_extender_1_out), .\dist ({5{1'b1}}), .out(shifter_1_out));
  Shifter #(.width(32), .shift("lr")) shifter_2 (.in(x), .\dist (5'b00001), .out(shifter_2_out));
  assign out = shifter_2_out | shifter_1_out;  // OR_Gate or_1, 32 bits wide
endmodule
