// Logisim project circ_test.circ as structural Verilog: 1 circuit, main circuit main
module main (
);

  wire main_1_equal, main_1_signed_overflow;
  wire [31:0] main_1_result, shifter_1_out;

  // Probe on main_1_equal
  // Probe on 32'he103
  alu_main main_1 (
    .Switch__S({6{1'b1}}), .X(32'h6ff), .Equal(main_1_equal), .RESULT(main_1_result),
    .Signed_Overflow(main_1_signed_overflow), .Y(32'h6fffffff));
  // Probe on main_1_signed_overflow
  // Probe on main_1_result
  Shifter #(.width(32), .shift("rr")) shifter_1 (.in(32'he103), .\dist (5'b01110), .out(shifter_1_out));
  // Probe on shifter_1_out
endmodule
