// Logisim project cpu.circ as structural Verilog: 18 circuits, main circuit main
module main (
  input  [31:0] RS_READ_VALUE,
  input  [31:0] RT_READ_VALUE,
  input  [31:0] INSTRUCTION,
  input  CLOCK,
  input  [23:0] C,
  input  RESET,
  output [4:0] RS,
  output [4:0] RT,
  output [4:0] Write_Register,
  output [31:0] RD_WRITE_VALUE,
  output RD_WRITE_ENABLE,
  output [23:0] FETCH_ADDRESS,
  output [31:0] t0,
  output [31:0] t1,
  output [31:0] t2,
  output [31:0] t3
);

  wire AluOp1, AluOp2, AluOp3, AluSrc, AluSrc_id_ex, and_1_out, and_2_out, beq, beq_id_ex, bne, bne_id_ex,
       Branch, branch_t, \byte , byte_ex_mem, byte_id_ex, control_1_aluop1, control_1_aluop2,
       control_1_aluop3, control_1_alusrc, control_1_beq, control_1_bne, control_1_byte, control_1_j,
       control_1_jl, control_1_lui, control_1_memread, control_1_memtoreg, control_1_memwrite,
       control_1_regdst, control_1_regwrite, control_1_u, DataHazard, IsRdT, IsRsT, IsRtT, j, j_id_ex, jl,
       jl_id_ex, Lui, Lui_ex_mem, Lui_id_ex, Lui_mem_wb, MemRead, MemRead_ex_mem, MemRead_id_ex, MemToReg,
       MemToReg_ex_mem, MemToReg_id_ex, MemToReg_mem_wb, MemWrite, MemWrite_ex_mem, MemWrite_id_ex,
       not_2_out, RegDst, RegDst_ex_mem, RegDst_id_ex, RegDst_mem_wb, RegWrite, RegWrite_ex_mem,
       RegWrite_id_ex, RegWrite_mem_wb, ShouldBranch, Stall, SwitchReg, SwitchReg_id_ex, u, u_ex_mem,
       u_id_ex, zero;
  wire [1:0] ForwardA, ForwardB, RdT, reg_choose_1_num, RsT, RtT;
  wire [4:0] rd, rd_ex_mem, rd_id_ex, rd_mem_wb, rs_t, rt_ex_mem, rt_t, shamt, WriteReg, WriteReg_ex_mem,
       WriteReg_id_ex;
  wire [5:0] aluop, aluop_id_ex, funct, funct_ex_mem, funct_id_ex, opcode;
  wire [23:0] pc_id_ex;
  wire [31:0] alu_module_1_result, imm, imm_ex_mem, imm_id_ex, imm_mem_wb, instr_ex_mem, instr_id_ex,
       instr_if_id, instr_if_id_t, instr_mem_wb, lrs, lrt, MemVal, MemVal_mem_wb, multiplexer_3_out,
       multiplexer_4_out, ReadRs, ReadRs_id_ex, ReadRt, ReadRt_id_ex, Result, Result_ex_mem, Result_mem_wb,
       wValue;

  // Probe on RD_WRITE_VALUE
  or or_1 (RD_WRITE_ENABLE, RegWrite_mem_wb, jl);
  control control_1 (
    .in_1(opcode), .RegDst(control_1_regdst), .AluSrc(control_1_alusrc), .MemToReg(control_1_memtoreg),
    .RegWrite(control_1_regwrite), .MemRead(control_1_memread), .MemWrite(control_1_memwrite),
    .beq(control_1_beq), .bne(control_1_bne), .AluOp1(control_1_aluop1), .AluOp2(control_1_aluop2),
    .AluOp3(control_1_aluop3), .Lui(control_1_lui), .\byte (control_1_byte), .u(control_1_u),
    .j(control_1_j), .jl(control_1_jl));
  reg_choose reg_choose_1 (.in_1(WriteReg), .num(reg_choose_1_num));  // open: isT
  reg_choose reg_choose_2 (.in_1(rs_t), .isT(IsRsT), .num(RsT));
  reg_choose reg_choose_3 (.in_1(rt_t), .isT(IsRtT), .num(RtT));
  reg_choose reg_choose_4 (.in_1(rd), .isT(IsRdT), .num(RdT));
  alu_control alu_control_1 (.aluOp0(AluOp1), .aluOp1(AluOp2), .aluOp2(AluOp3), .funct(funct), .out(aluop));
  regfile_main RegFile (
    .Read_register_1(RsT), .Read_register_2(RtT), .write_register(reg_choose_1_num), .write_data(wValue),
    .t0_Value(t0), .t1_Value(t1), .t2_Value(t2), .t3_Value(t3), .RegWrite(RegWrite), .clock(CLOCK),
    .Read_Data_1(lrs), .Read_Data_2(lrt));
  // Probe on RT_READ_VALUE
  // Probe on INSTRUCTION
  Multiplexer #(.width(32)) multiplexer_1 (.in0(RS_READ_VALUE), .in1(lrs), .out(ReadRs), .sel(IsRsT));  // open: en
  Multiplexer #(.width(32)) multiplexer_2 (.in0(RT_READ_VALUE), .in1(lrt), .out(ReadRt), .sel(IsRtT));  // open: en
  // NOT_Gate not_1 is placed but not wired
  // Probe on ForwardB
  // Probe on C
  // Probe on instr_if_id_t
  IF_ID if_id_1 (.instr(INSTRUCTION), .clk(CLOCK), .instr_2(instr_if_id_t), .Stall(DataHazard));  // open: PC, PC_2
  HazardControl hazardcontrol_1 (
    .RegDst0(control_1_regdst), .AluSrc(control_1_alusrc), .MemToReg(control_1_memtoreg),
    .RegWrite(control_1_regwrite), .MemRead(control_1_memread), .MemWrite(control_1_memwrite),
    .beq(control_1_beq), .bne(control_1_bne), .Lui(control_1_aluop1), .AluOp1(control_1_aluop2),
    .AluOp2(control_1_aluop3), .AluOp3(control_1_lui), .\byte (control_1_byte), .u(control_1_u),
    .j(control_1_j), .jl(control_1_jl), .Stall(Stall), .RegDst(RegDst), .AluSrc_2(AluSrc),
    .MemToReg_2(MemToReg), .RegWrite_2(RegWrite), .MemRead_2(MemRead), .MemWrite_2(MemWrite), .beq_2(beq),
    .bne_2(bne), .Lui_2(AluOp1), .AluOp1_2(AluOp2), .AluOp2_2(AluOp3), .AluOp3_2(Lui), .byte_2(\byte ),
    .u_2(u), .j_2(j), .jl_2(jl));
  Multiplexer #(.select(2), .width(32)) multiplexer_3 (
    .in0(ReadRs), .in1(RD_WRITE_VALUE), .in2(Result_ex_mem), .out(multiplexer_3_out), .sel(ForwardA));  // open: in3, en
  // Probe on ForwardA
  Multiplexer #(.select(2), .width(32)) multiplexer_4 (
    .in0(ReadRt), .in1(wValue), .in2(Result_ex_mem), .out(multiplexer_4_out), .sel(ForwardB));  // open: in3, en
  or or_2 (Stall, DataHazard, ShouldBranch);
  // Probe on multiplexer_3_out
  // Probe on multiplexer_4_out
  Multiplexer #(.width(32)) multiplexer_5 (
    .in0(instr_if_id_t), .in1({32{1'b0}}), .out(instr_if_id), .sel(Stall));  // open: en
  HazDetectionUnit hazdetectionunit_1 (
    .MemRead(MemRead_id_ex), .rt_id_ex(RT), .rt_if_id(rt_t), .rs_if_id(rs_t), .out(DataHazard));
  // Probe on instr_if_id_t
  Alu_module alu_module_1 (
    .readRs(multiplexer_3_out), .readRt(multiplexer_4_out), .imm(imm_id_ex), .aluop(aluop_id_ex),
    .AluSrc(AluSrc_id_ex), .SwitchReg(SwitchReg_id_ex), .result(alu_module_1_result), .zero(zero));  // open: signedOverflow
  or or_3 (branch_t, bne, beq);
  split_instruction split_instruction_1 (
    .in_1(instr_if_id_t), .opcode(opcode), .rs(rs_t), .rt(rt_t), .rd(rd), .shamt(shamt), .funct(funct),
    .imm(imm), .SwitchReg(SwitchReg));
  mem_module mem_module_1 (
    .Data_Mem_Addr(Result_ex_mem), .Data_Mem_In(ReadRt_id_ex), .write(MemWrite_id_ex), .clk(CLOCK),
    .\byte (byte_ex_mem), .u(u_ex_mem), .out(MemVal));
  ID_EX id_ex_1 (
    .WriteReg0(WriteReg), .AluOp(aluop), .funct(funct), .RegDst(RegDst), .AluSrc(AluSrc), .MemRead(MemRead),
    .MemWrite(MemWrite), .Branch(Branch), .Data1(ReadRs), .Data2(ReadRt), .PC(FETCH_ADDRESS), .imm(imm),
    .rt(rt_t), .rd(rd), .MemToReg(MemToReg), .SwitchReg(SwitchReg), .Lui(Lui), .\byte (\byte ), .u(u), .j(j),
    .jl(jl), .regWrite(RegWrite), .rs(rs_t), .beq(beq), .bne(bne), .instr(instr_if_id), .clk(CLOCK),
    .WriteReg(WriteReg_id_ex), .AluOp_2(aluop_id_ex), .funct_2(funct_id_ex), .RegDst_2(RegDst_id_ex),
    .AluSrc_2(AluSrc_id_ex), .MemRead_2(MemRead_id_ex), .MemWrite_2(MemWrite_id_ex), .Branch_2(Branch),
    .Data1_2(ReadRs_id_ex), .Data2_2(ReadRt_id_ex), .PC_2(pc_id_ex), .imm_2(imm_id_ex), .rt_2(RT),
    .rd_2(rd_id_ex), .MemToReg_2(MemToReg_id_ex), .SwitchReg_2(SwitchReg_id_ex), .Lui_2(Lui_id_ex),
    .byte_2(byte_id_ex), .u_2(u_id_ex), .j_2(j_id_ex), .jl_2(jl_id_ex), .regWrite_2(RegWrite_id_ex),
    .rs_2(RS), .beq_2(beq_id_ex), .bne_2(bne_id_ex), .instr_2(instr_id_ex));
  // Probe on nothing
  AluSub alusub_1 (
    .PC(FETCH_ADDRESS), .rdValue(alu_module_1_result), .imm(imm_id_ex), .Lui(Lui_id_ex), .jl(jl),
    .wValue(Result));
  and and_1 (and_1_out, beq_id_ex, zero);
  not not_2 (not_2_out, zero);
  Multiplexer #(.width(32)) multiplexer_6 (
    .in0(Result_mem_wb), .in1(MemVal_mem_wb), .out(RD_WRITE_VALUE), .sel(MemToReg_mem_wb));  // open: en
  pc_logic pc_logic_1 (
    .branch(ShouldBranch), .imm(imm_id_ex), .j(j), .stall(DataHazard), .pc_branch(pc_id_ex), .clk(CLOCK),
    .out(FETCH_ADDRESS));
  and and_2 (and_2_out, bne_id_ex, not_2_out);
  // Probe on RD_WRITE_VALUE
  or or_4 (ShouldBranch, and_1_out, and_2_out);
  // Probe on instr_id_ex
  EX_MEM ex_mem_1 (
    .WriteReg0(WriteReg_id_ex), .funct(funct_id_ex), .RegDst(RegDst_id_ex), .MemRead(MemRead_id_ex),
    .MemWrite(MemWrite_id_ex), .MemToReg(MemToReg_id_ex), .imm(imm_id_ex), .u(u_id_ex), .\byte (byte_id_ex),
    .lui(Lui_id_ex), .regWrite(RegWrite_id_ex), .rt(RT), .rd(rd_id_ex), .Addr(Result), .instr(instr_id_ex),
    .clk(CLOCK), .WriteReg(WriteReg_ex_mem), .funct_2(funct_ex_mem), .RegDst_2(RegDst_ex_mem),
    .MemRead_2(MemRead_ex_mem), .MemWrite_2(MemWrite_ex_mem), .MemToReg_2(MemToReg_ex_mem),
    .imm_2(imm_ex_mem), .u_2(u_ex_mem), .byte_2(byte_ex_mem), .lui_2(Lui_ex_mem),
    .regWrite_2(RegWrite_ex_mem), .rt_2(rt_ex_mem), .rd_2(rd_ex_mem), .Addr_2(Result_ex_mem),
    .instr_2(instr_ex_mem));
  mem_wb mem_wb_1 (
    .WriteReg0(WriteReg_ex_mem), .RegDst(RegDst_ex_mem), .MemToReg(MemToReg_ex_mem),
    .RegWrite(RegWrite_ex_mem), .imm(imm_ex_mem), .Result(Result_ex_mem), .MemVal(MemVal), .rd(rd_ex_mem),
    .lui(Lui_ex_mem), .instr(instr_ex_mem), .clk(CLOCK), .WriteReg(Write_Register), .RegDst_2(RegDst_mem_wb),
    .MemToReg_2(MemToReg_mem_wb), .RegWrite_2(RegWrite_mem_wb), .imm_2(imm_mem_wb), .Result_2(Result_mem_wb),
    .MemVal_2(MemVal_mem_wb), .rd_2(rd_mem_wb), .lui_2(Lui_mem_wb), .instr_2(instr_mem_wb));
  ForwardUnit forwardunit_1 (
    .RegWrite_ex_mem(RegWrite_ex_mem), .rs_id_ex(RS), .rt_id_ex(RT), .rd_ex_mem(WriteReg_ex_mem),
    .rd_mem_wb(Write_Register), .RegWrite_mem_wb(RegWrite_mem_wb), .ForwardA(ForwardA), .ForwardB(ForwardB));
  // Probe on instr_ex_mem
  write_reg_choose write_reg_choose_1 (.rt(rt_t), .rd(rd), .regDst(RegDst), .jl(jl), .writeReg(WriteReg));
  // Probe on instr_mem_wb
  // Probe on nothing

  // Other names for the same wires on the sheet: clk = CLOCK; instr[31:0] = INSTRUCTION; pc[23:0] = FETCH_ADDRESS;
  //   rdValue[31:0] = RD_WRITE_VALUE; rs_id_ex[4:0] = RS; rt_id_ex[4:0] = RT; WriteReg_mem_wb[4:0] = Write_Register

  // Notes on the sheet:
  //   These are outputs/inputs from run.circ
  //   These are outputs to run.circ
  //   Decode
  //   t Registers
  //   EX/Mem
  //   Branch logic
endmodule

module control (
  input  [5:0] in_1,
  output RegDst,
  output AluSrc,
  output MemToReg,
  output RegWrite,
  output MemRead,
  output MemWrite,
  output beq,
  output bne,
  output AluOp1,
  output AluOp2,
  output AluOp3,
  output Lui,
  output \byte ,
  output u,
  output j,
  output jl
);

  wire and_2_out, and_3_out, bitselector_1_out, bitselector_2_out, bitselector_3_out, bitselector_4_out,
       bitselector_5_out, bitselector_6_out, bitselector_7_out, bitselector_8_out, bitselector_9_out,
       comparator_4_eq, comparator_5_eq, comparator_6_eq, comparator_12_eq, comparator_14_eq, isAdd, isAnd,
       isOr, isSub, j_t, not_1_out, not_2_out, not_3_out, not_4_out;
  wire [5:0] and_1_out;

  Comparator #(.width(6)) comparator_1 (.a({6{1'b0}}), .b(in_1), .eq(AluOp3));  // open: gt, lt
  Comparator #(.width(6)) comparator_2 (.a({6{1'b0}}), .b(in_1), .eq(RegDst));  // open: gt, lt
  assign and_1_out = in_1 & 6'b101000;  // AND_Gate and_1, 6 bits wide
  Comparator #(.width(6), .mode("unsigned")) comparator_3 (.a(and_1_out), .b({6{1'b0}}), .gt(AluSrc));  // open: eq, lt
  or or_1 (RegWrite, RegDst, AluSrc);
  Comparator #(.width(6)) comparator_4 (.a(6'b100000), .b(in_1), .eq(comparator_4_eq));  // open: gt, lt
  Comparator #(.width(6)) comparator_5 (.a(6'b100100), .b(in_1), .eq(comparator_5_eq));  // open: gt, lt
  Comparator #(.width(6)) comparator_6 (.a(6'b100011), .b(in_1), .eq(comparator_6_eq));  // open: gt, lt
  Comparator #(.width(6)) comparator_7 (.a(6'b101011), .b(in_1), .eq(MemWrite));  // open: gt, lt
  Comparator #(.width(6)) comparator_8 (.a(6'b000010), .b(in_1), .eq(j_t));  // open: gt, lt
  Comparator #(.width(6)) comparator_9 (.a(6'b000011), .b(in_1), .eq(jl));  // open: gt, lt
  or or_2 (MemRead, comparator_4_eq, comparator_5_eq, comparator_6_eq);
  Comparator #(.width(6)) comparator_10 (.a(6'b000100), .b(in_1), .eq(beq));  // open: gt, lt
  Comparator #(.width(6)) comparator_11 (.a(6'b000101), .b(in_1), .eq(bne));  // open: gt, lt
  BitSelector #(.width(6)) bitselector_1 (.in(in_1), .out(bitselector_1_out), .sel(3'b101));
  not not_1 (not_1_out, bitselector_2_out);
  BitSelector #(.width(6)) bitselector_2 (.in(in_1), .out(bitselector_2_out), .sel(3'b010));
  BitSelector #(.width(6)) bitselector_3 (.in(in_1), .out(bitselector_3_out), .sel(3'b011));
  BitSelector #(.width(6)) bitselector_4 (.in(in_1), .out(bitselector_4_out), .sel(3'b000));
  BitSelector #(.width(6)) bitselector_5 (.in(in_1), .out(bitselector_5_out), .sel(3'b010));
  BitSelector #(.width(6)) bitselector_6 (.in(in_1), .out(bitselector_6_out), .sel(3'b011));
  or or_3 (isAdd, bitselector_1_out, and_2_out);
  and and_2 (and_2_out, not_1_out, bitselector_3_out);
  BitSelector #(.width(6)) bitselector_7 (.in(in_1), .out(bitselector_7_out), .sel(3'b010));
  BitSelector #(.width(6)) bitselector_8 (.in(in_1), .out(bitselector_8_out), .sel(3'b101));
  BitSelector #(.width(6)) bitselector_9 (.in(in_1), .out(bitselector_9_out), .sel(3'b011));
  not not_2 (not_2_out, bitselector_4_out);
  and and_3 (and_3_out, bitselector_5_out, bitselector_6_out);
  Comparator #(.width(6)) comparator_12 (.a(6'b100000), .b(in_1), .eq(comparator_12_eq));  // open: gt, lt
  Comparator #(.width(6)) comparator_13 (.a(6'b100100), .b(in_1), .eq(u));  // open: gt, lt
  Comparator #(.width(6)) comparator_14 (.a(6'b101000), .b(in_1), .eq(comparator_14_eq));  // open: gt, lt
  not not_3 (not_3_out, bitselector_8_out);
  not not_4 (not_4_out, bitselector_9_out);
  and and_4 (isAnd, not_2_out, and_3_out);
  or or_4 (\byte , comparator_12_eq, u, comparator_14_eq);
  and and_5 (isSub, bitselector_7_out, not_3_out, not_4_out);
  and and_6 (isOr, bitselector_4_out, and_3_out);
  or or_5 (AluOp1, isSub, AluOp3, isOr);
  or or_6 (AluOp2, isOr, AluOp3, isAnd);
  or or_7 (j, j_t, jl);
  Comparator #(.width(6)) comparator_15 (.a(in_1), .b(6'b001111), .eq(Lui));  // open: gt, lt

  assign MemToReg = MemRead;

  // Other names for the same wires on the sheet: isR = AluOp3; opcode[5:0] = in_1
endmodule

module split_instruction (
  input  [31:0] in_1,
  output [5:0] opcode,
  output [4:0] rs,
  output [4:0] rt,
  output [4:0] rd,
  output [4:0] shamt,
  output [5:0] funct,
  output [31:0] imm,
  output SwitchReg
);

  wire comparator_1_eq, comparator_2_eq, comparator_3_eq, comparator_4_lt, comparator_5_eq, comparator_6_eq,
       comparator_7_eq, j, zeroImm;
  wire [15:0] bit_extender_5_out;
  wire [31:0] and_2_out, and_3_out, and_4_out, and_5_out, and_6_out, and_7_out, bit_extender_6_out,
       bit_extender_7_out, imm_t, jimm, multiplexer_2_out, shamt32, shifter_1_out, shifter_2_out,
       shifter_3_out, shifter_4_out, shifter_5_out;

  assign shamt32 = 32'h1f & shifter_1_out;  // AND_Gate and_1, 32 bits wide
  Shifter #(.width(32), .shift("lr")) shifter_1 (.in(in_1), .\dist (5'b00110), .out(shifter_1_out));
  assign and_2_out = 32'h1f & shifter_2_out;  // AND_Gate and_2, 32 bits wide
  Shifter #(.width(32), .shift("lr")) shifter_2 (.in(in_1), .\dist (5'b01011), .out(shifter_2_out));
  assign and_3_out = 32'h1f & shifter_3_out;  // AND_Gate and_3, 32 bits wide
  Shifter #(.width(32), .shift("lr")) shifter_3 (.in(in_1), .\dist (5'b10000), .out(shifter_3_out));
  Comparator #(.width(6), .mode("unsigned")) comparator_1 (
    .a(opcode), .b(6'b001101), .eq(comparator_1_eq));  // open: gt, lt
  Comparator #(.width(6), .mode("unsigned")) comparator_2 (
    .a(opcode), .b(6'b001100), .eq(comparator_2_eq));  // open: gt, lt
  Bit_Extender #(.in_width(32), .out_width(6)) bit_extender_1 (.in(and_4_out), .out(funct));
  assign and_4_out = 32'h3f & in_1;  // AND_Gate and_4, 32 bits wide
  Bit_Extender #(.in_width(32), .out_width(5)) bit_extender_2 (.in(shamt32), .out(shamt));
  Bit_Extender #(.in_width(32), .out_width(5)) bit_extender_3 (.in(and_2_out), .out(rd));
  Bit_Extender #(.in_width(32), .out_width(5)) bit_extender_4 (.in(and_3_out), .out(rt));
  or or_1 (zeroImm, comparator_1_eq, comparator_2_eq);
  Bit_Extender #(.in_width(32), .\type ("sign")) bit_extender_5 (.in(in_1), .out(bit_extender_5_out));
  Shifter #(.width(32), .shift("lr")) shifter_4 (.in(in_1), .\dist (5'b10101), .out(shifter_4_out));
  Shifter #(.width(32), .shift("lr")) shifter_5 (.in(in_1), .\dist (5'b11010), .out(shifter_5_out));
  Multiplexer #(.width(32)) multiplexer_1 (
    .in0(bit_extender_7_out), .in1(bit_extender_6_out), .out(imm_t), .sel(zeroImm));  // open: en
  assign bit_extender_6_out = {{16{1'b0}}, bit_extender_5_out};  // Bit_Extender bit_extender_6
  assign bit_extender_7_out = {{16{bit_extender_5_out[15]}}, bit_extender_5_out};  // Bit_Extender bit_extender_7
  assign and_5_out = 32'h1f & shifter_4_out;  // AND_Gate and_5, 32 bits wide
  Bit_Extender #(.in_width(32), .out_width(5)) bit_extender_8 (.in(and_5_out), .out(rs));
  Bit_Extender #(.in_width(32), .out_width(6)) bit_extender_9 (.in(and_6_out), .out(opcode));
  assign and_6_out = 32'h3f & shifter_5_out;  // AND_Gate and_6, 32 bits wide
  assign and_7_out = 32'hffff & in_1;  // AND_Gate and_7, 32 bits wide
  Comparator #(.width(6), .mode("unsigned")) comparator_3 (
    .a(opcode), .b({6{1'b0}}), .eq(comparator_3_eq));  // open: gt, lt
  Comparator #(.width(6), .mode("unsigned")) comparator_4 (
    .a(funct), .b(6'b000100), .lt(comparator_4_lt));  // open: gt, eq
  Comparator #(.width(6), .mode("unsigned")) comparator_5 (
    .a(opcode), .b(6'b000010), .eq(comparator_5_eq));  // open: gt, lt
  Comparator #(.width(6), .mode("unsigned")) comparator_6 (
    .a(opcode), .b(6'b000011), .eq(comparator_6_eq));  // open: gt, lt
  or or_2 (j, comparator_5_eq, comparator_6_eq);
  Multiplexer #(.width(32)) multiplexer_2 (
    .in0(imm_t), .in1(shamt32), .out(multiplexer_2_out), .sel(comparator_7_eq));  // open: en
  Comparator #(.width(6), .mode("unsigned")) comparator_7 (
    .a(opcode), .b({6{1'b0}}), .eq(comparator_7_eq));  // open: gt, lt
  and and_8 (SwitchReg, comparator_3_eq, comparator_4_lt);
  Multiplexer #(.width(32)) multiplexer_3 (.in0(multiplexer_2_out), .in1(jimm), .out(imm), .sel(j));  // open: en
  assign jimm = 32'h3ffffff & in_1;  // AND_Gate and_9, 32 bits wide

  // Other names for the same wires on the sheet: in[31:0] = in_1
endmodule

module reg_choose (
  input  [4:0] in_1,
  output isT,
  output [1:0] num
);

  wire bitselector_1_out, bitselector_2_out, second_out;
  wire [4:0] subtractor_1_out;

  BitSelector #(.width(5)) bitselector_1 (.in(in_1), .out(bitselector_1_out), .sel(3'b010));
  BitSelector #(.width(5)) bitselector_2 (.in(in_1), .out(bitselector_2_out), .sel(3'b011));
  not second (second_out, bitselector_1_out);
  Subtractor #(.width(5)) subtractor_1 (.a(in_1), .b(5'b01000), .out(subtractor_1_out));  // open: bin, bout
  and and_1 (isT, second_out, bitselector_2_out);
  Bit_Extender #(.in_width(5), .out_width(2)) bit_extender_1 (.in(subtractor_1_out), .out(num));
endmodule

// PC
module pc_logic (
  input  branch,
  input  [31:0] imm,
  input  j,
  input  stall,
  input  [23:0] pc_branch,
  input  clk,
  output [23:0] out
);

  wire not_1_out;
  wire [23:0] subtractor_1_out;
  wire [31:0] adder_1_out, adder_2_out, adder_3_out, and_1_out, bit_extender_1_out, jaddr, multiplexer_1_out,
       multiplexer_2_out, multiplexer_3_out, register_1_q;

  not not_1 (not_1_out, stall);
  Register #(.width(32)) register_1 (.D(adder_1_out), .en(not_1_out), .Q(register_1_q), .clk(clk));  // open: clr
  Adder #(.width(32)) adder_1 (.a(32'h1), .b(register_1_q), .out(adder_1_out));  // open: cin, cout
  Shifter #(.width(32)) shifter_1 (.in(imm), .\dist (5'b00010));  // open: out
  Subtractor #(.width(24)) subtractor_1 (.a(pc_branch), .b(24'h1), .out(subtractor_1_out));  // open: bin, bout
  Subtractor #(.width(32)) subtractor_2 (.a(imm), .b(32'h100000), .out(jaddr));  // open: bin, bout
  assign bit_extender_1_out = {{8{subtractor_1_out[23]}}, subtractor_1_out};  // Bit_Extender bit_extender_1
  Multiplexer #(.width(32)) multiplexer_1 (
    .in0(register_1_q), .in1(jaddr), .out(multiplexer_1_out), .sel(j));  // open: en
  Adder #(.width(32)) adder_2 (.a(32'h1), .b(bit_extender_1_out), .out(adder_2_out));  // open: cin, cout
  Multiplexer #(.width(32)) multiplexer_2 (
    .in0(multiplexer_1_out), .in1(multiplexer_3_out), .out(multiplexer_2_out), .sel(branch));  // open: en
  assign and_1_out = adder_2_out & {32{1'b1}};  // AND_Gate and_1, 32 bits wide
  Bit_Extender #(.in_width(32), .out_width(24), .\type ("sign")) bit_extender_2 (.in(multiplexer_2_out), .out(out));
  Adder #(.width(32)) adder_3 (.a(and_1_out), .b(imm), .out(adder_3_out));  // open: cin, cout
  Multiplexer #(.width(32)) multiplexer_3 (
    .in0(adder_2_out), .in1(adder_3_out), .out(multiplexer_3_out), .sel(branch));  // open: en
  // NOT_Gate not_2 is placed but not wired
endmodule

module alu_control (
  input  aluOp0,
  input  aluOp1,
  input  aluOp2,
  input  [5:0] funct,
  output [5:0] out
);

  wire [2:0] _0, _1, _2, or_1_out, shifter_1_out, shifter_2_out;

  assign _0 = {{2{1'b0}}, aluOp0};  // Bit_Extender bit_extender_1
  assign _1 = {{2{1'b0}}, aluOp1};  // Bit_Extender bit_extender_2
  assign _2 = {{2{1'b0}}, aluOp2};  // Bit_Extender bit_extender_3
  Shifter #(.width(3)) shifter_1 (.in(_1), .\dist (2'b01), .out(shifter_1_out));
  Shifter #(.width(3)) shifter_2 (.in(_2), .\dist (2'b10), .out(shifter_2_out));
  assign or_1_out = _0 | shifter_1_out | shifter_2_out;  // OR_Gate or_1, 3 bits wide
  Multiplexer #(.select(3), .width(6)) multiplexer_1 (
    .in0(6'b100000), .in1(6'b100010), .in2(6'b100100), .in3(6'b100101), .in7(funct), .out(out), .sel(or_1_out));  // open: in4, in5, in6, en
endmodule

module Alu_module (
  input  [31:0] readRs,
  input  [31:0] readRt,
  input  [31:0] imm,
  input  [5:0] aluop,
  input  AluSrc,
  input  SwitchReg,
  output [31:0] result,
  output signedOverflow,
  output zero
);

  wire or_1_out;
  wire [31:0] multiplexer_1_out, multiplexer_2_out;

  Multiplexer #(.width(32)) multiplexer_1 (
    .in0(readRs), .in1(readRt), .out(multiplexer_1_out), .sel(SwitchReg));  // open: en
  Multiplexer #(.width(32)) multiplexer_2 (
    .in0(readRt), .in1(imm), .out(multiplexer_2_out), .sel(or_1_out));  // open: en
  or or_1 (or_1_out, SwitchReg, AluSrc);
  alu_main ALU (
    .Switch__S(aluop), .X(multiplexer_1_out), .Equal(zero), .RESULT(result),
    .Signed_Overflow(signedOverflow), .Y(multiplexer_2_out));
endmodule

module mem_module (
  input  [31:0] Data_Mem_Addr,
  input  [31:0] Data_Mem_In,
  input  write,
  input  clk,
  input  \byte ,
  input  u,
  output [31:0] out
);

  wire and_1_out, not_1_out;
  wire [7:0] bit_extender_1_out;
  wire [31:0] bit_extender_2_out, main_1_data_mem_out;

  mem_main main_1 (
    .Data_Mem_Addr(Data_Mem_Addr), .Data_Mem_In(Data_Mem_In), .ACCESS_BYTE(\byte ), .MEM_WRITE(write),
    .CLOCK(clk), .Data_Mem_Out(main_1_data_mem_out));
  Bit_Extender #(.in_width(32), .out_width(8), .\type ("sign")) bit_extender_1 (
    .in(main_1_data_mem_out), .out(bit_extender_1_out));
  assign bit_extender_2_out = {{24{bit_extender_1_out[7]}}, bit_extender_1_out};  // Bit_Extender bit_extender_2
  not not_1 (not_1_out, u);
  Multiplexer #(.width(32)) multiplexer_1 (
    .in0(main_1_data_mem_out), .in1(bit_extender_2_out), .out(out), .sel(and_1_out));  // open: en
  and and_1 (and_1_out, not_1_out, \byte );

  // Other names for the same wires on the sheet: MemWrite = write
endmodule

module write_reg_choose (
  input  [4:0] rt,
  input  [4:0] rd,
  input  regDst,
  input  jl,
  output [4:0] writeReg
);

  wire [4:0] multiplexer_1_out;

  Multiplexer #(.width(5)) multiplexer_1 (.in0(rt), .in1(rd), .out(multiplexer_1_out), .sel(regDst));  // open: en
  Multiplexer #(.width(5)) multiplexer_2 (
    .in0(multiplexer_1_out), .in1({5{1'b1}}), .out(writeReg), .sel(jl));  // open: en
endmodule

module IF_ID (
  input  [31:0] instr,
  input  Stall,
  input  [23:0] PC,
  input  clk,
  output [31:0] instr_2,
  output [23:0] PC_2
);

  wire not_1_out;

  not not_1 (not_1_out, Stall);
  Register #(.width(32)) register_1 (.D(instr), .en(not_1_out), .Q(instr_2), .clk(clk));  // open: clr
  Register #(.width(24)) register_2 (.D(PC), .en(not_1_out), .Q(PC_2), .clk(clk));  // open: clr
endmodule

// id/ex
module ID_EX (
  input  [4:0] WriteReg0,
  input  [5:0] AluOp,
  input  [5:0] funct,
  input  RegDst,
  input  AluSrc,
  input  MemRead,
  input  MemWrite,
  input  Branch,
  input  [31:0] Data1,
  input  [31:0] Data2,
  input  [23:0] PC,
  input  [31:0] imm,
  input  [4:0] rt,
  input  [4:0] rd,
  input  MemToReg,
  input  SwitchReg,
  input  Lui,
  input  \byte ,
  input  u,
  input  j,
  input  jl,
  input  regWrite,
  input  [4:0] rs,
  input  beq,
  input  bne,
  input  [31:0] instr,
  input  clk,
  output [4:0] WriteReg,
  output [5:0] AluOp_2,
  output [5:0] funct_2,
  output RegDst_2,
  output AluSrc_2,
  output MemRead_2,
  output MemWrite_2,
  output Branch_2,
  output [31:0] Data1_2,
  output [31:0] Data2_2,
  output [23:0] PC_2,
  output [31:0] imm_2,
  output [4:0] rt_2,
  output [4:0] rd_2,
  output MemToReg_2,
  output SwitchReg_2,
  output Lui_2,
  output byte_2,
  output u_2,
  output j_2,
  output jl_2,
  output regWrite_2,
  output [4:0] rs_2,
  output beq_2,
  output bne_2,
  output [31:0] instr_2
);

  Register #(.width(5)) register_1 (.D(WriteReg0), .Q(WriteReg), .clk(clk));  // open: en, clr
  Register #(.width(6)) register_2 (.D(AluOp), .Q(AluOp_2), .clk(clk));  // open: en, clr
  Register #(.width(6)) register_3 (.D(funct), .Q(funct_2), .clk(clk));  // open: en, clr
  Register #(.width(1)) register_4 (.D(RegDst), .Q(RegDst_2), .clk(clk));  // open: en, clr
  Register #(.width(1)) register_5 (.D(AluSrc), .Q(AluSrc_2), .clk(clk));  // open: en, clr
  Register #(.width(1)) register_6 (.D(MemRead), .Q(MemRead_2), .clk(clk));  // open: en, clr
  Register #(.width(1)) register_7 (.D(MemWrite), .Q(MemWrite_2), .clk(clk));  // open: en, clr
  Register #(.width(1)) register_8 (.D(Branch), .Q(Branch_2), .clk(clk));  // open: en, clr
  Register #(.width(32)) register_9 (.D(Data1), .Q(Data1_2), .clk(clk));  // open: en, clr
  Register #(.width(32)) register_10 (.D(Data2), .Q(Data2_2), .clk(clk));  // open: en, clr
  Register #(.width(24)) register_11 (.D(PC), .Q(PC_2), .clk(clk));  // open: en, clr
  Register #(.width(32)) register_12 (.D(imm), .Q(imm_2), .clk(clk));  // open: en, clr
  Register #(.width(5)) register_13 (.D(rt), .Q(rt_2), .clk(clk));  // open: en, clr
  Register #(.width(5)) register_14 (.D(rd), .Q(rd_2), .clk(clk));  // open: en, clr
  Register #(.width(1)) register_15 (.D(MemToReg), .Q(MemToReg_2), .clk(clk));  // open: en, clr
  Register #(.width(1)) register_16 (.D(SwitchReg), .Q(SwitchReg_2), .clk(clk));  // open: en, clr
  Register #(.width(1)) register_17 (.D(Lui), .Q(Lui_2), .clk(clk));  // open: en, clr
  Register #(.width(1)) register_18 (.D(\byte ), .Q(byte_2), .clk(clk));  // open: en, clr
  Register #(.width(1)) register_19 (.D(u), .Q(u_2), .clk(clk));  // open: en, clr
  Register #(.width(1)) register_20 (.D(j), .Q(j_2), .clk(clk));  // open: en, clr
  Register #(.width(1)) register_21 (.D(jl), .Q(jl_2), .clk(clk));  // open: en, clr
  Register #(.width(1)) register_22 (.D(regWrite), .Q(regWrite_2), .clk(clk));  // open: en, clr
  Register #(.width(5)) register_23 (.D(rs), .Q(rs_2), .clk(clk));  // open: en, clr
  Register #(.width(1)) register_24 (.D(beq), .Q(beq_2), .clk(clk));  // open: en, clr
  Register #(.width(1)) register_25 (.D(bne), .Q(bne_2), .clk(clk));  // open: en, clr
  Register #(.width(32)) register_26 (.D(instr), .Q(instr_2), .clk(clk));  // open: en, clr
endmodule

// ex/mem
module EX_MEM (
  input  [4:0] WriteReg0,
  input  [5:0] funct,
  input  RegDst,
  input  MemRead,
  input  MemWrite,
  input  MemToReg,
  input  [31:0] imm,
  input  u,
  input  \byte ,
  input  lui,
  input  regWrite,
  input  [4:0] rt,
  input  [4:0] rd,
  input  [31:0] Addr,
  input  [31:0] instr,
  input  clk,
  output [4:0] WriteReg,
  output [5:0] funct_2,
  output RegDst_2,
  output MemRead_2,
  output MemWrite_2,
  output MemToReg_2,
  output [31:0] imm_2,
  output u_2,
  output byte_2,
  output lui_2,
  output regWrite_2,
  output [4:0] rt_2,
  output [4:0] rd_2,
  output [31:0] Addr_2,
  output [31:0] instr_2
);

  Register #(.width(5)) register_1 (.D(WriteReg0), .Q(WriteReg), .clk(clk));  // open: en, clr
  Register #(.width(6)) register_2 (.D(funct), .Q(funct_2), .clk(clk));  // open: en, clr
  Register #(.width(1)) register_3 (.D(RegDst), .Q(RegDst_2), .clk(clk));  // open: en, clr
  Register #(.width(1)) register_4 (.D(MemRead), .Q(MemRead_2), .clk(clk));  // open: en, clr
  Register #(.width(1)) register_5 (.D(MemWrite), .Q(MemWrite_2), .clk(clk));  // open: en, clr
  Register #(.width(1)) register_6 (.D(MemToReg), .Q(MemToReg_2), .clk(clk));  // open: en, clr
  Register #(.width(32)) register_7 (.D(imm), .Q(imm_2), .clk(clk));  // open: en, clr
  Register #(.width(1)) register_8 (.D(u), .Q(u_2), .clk(clk));  // open: en, clr
  Register #(.width(1)) register_9 (.D(\byte ), .Q(byte_2), .clk(clk));  // open: en, clr
  Register #(.width(1)) register_10 (.D(lui), .Q(lui_2), .clk(clk));  // open: en, clr
  Register #(.width(1)) register_11 (.D(regWrite), .Q(regWrite_2), .clk(clk));  // open: en, clr
  Register #(.width(5)) register_12 (.D(rt), .Q(rt_2), .clk(clk));  // open: en, clr
  Register #(.width(5)) register_13 (.D(rd), .Q(rd_2), .clk(clk));  // open: en, clr
  Register #(.width(32)) register_14 (.D(Addr), .Q(Addr_2), .clk(clk));  // open: en, clr
  Register #(.width(32)) register_15 (.D(instr), .Q(instr_2), .clk(clk));  // open: en, clr
endmodule

// mem/wb
module Mem_WB (
  input  [4:0] WriteReg0,
  input  RegDst,
  input  MemToReg,
  input  RegWrite,
  input  [31:0] imm,
  input  [31:0] Result,
  input  [31:0] MemVal,
  input  [4:0] rd,
  input  clk,
  output [4:0] WriteReg,
  output RegDst_2,
  output MemToReg_2,
  output RegWrite_2,
  output [31:0] imm_2,
  output [31:0] Result_2,
  output [31:0] MemVal_2,
  output [4:0] rd_2
);

  Register #(.width(5)) register_1 (.D(WriteReg0), .Q(WriteReg), .clk(clk));  // open: en, clr
  Register #(.width(1)) register_2 (.D(RegDst), .Q(RegDst_2), .clk(clk));  // open: en, clr
  Register #(.width(1)) register_3 (.D(MemToReg), .Q(MemToReg_2), .clk(clk));  // open: en, clr
  Register #(.width(1)) register_4 (.D(RegWrite), .Q(RegWrite_2), .clk(clk));  // open: en, clr
  Register #(.width(32)) register_5 (.D(imm), .Q(imm_2), .clk(clk));  // open: en, clr
  Register #(.width(32)) register_6 (.D(Result), .Q(Result_2), .clk(clk));  // open: en, clr
  Register #(.width(32)) register_7 (.D(MemVal), .Q(MemVal_2), .clk(clk));  // open: en, clr
  Register #(.width(5)) register_8 (.D(rd), .Q(rd_2), .clk(clk));  // open: en, clr
endmodule

module ForwardUnit (
  input  RegWrite_ex_mem,
  input  [4:0] rs_id_ex,
  input  [4:0] rt_id_ex,
  input  [4:0] rd_ex_mem,
  input  [4:0] rd_mem_wb,
  input  RegWrite_mem_wb,
  output [1:0] ForwardA,
  output [1:0] ForwardB
);

  wire comparator_1_eq, comparator_2_eq, comparator_3_eq, comparator_4_eq, comparator_5_eq, comparator_6_eq,
       comparator_7_eq, ForwardA01, ForwardA10, ForwardB01, ForwardB10, not_1_out, not_2_out, not_3_out;
  wire [1:0] adder_1_out, adder_2_out, bit_extender_1_out, bit_extender_2_out, bit_extender_3_out,
       bit_extender_4_out, shifter_1_out, shifter_2_out;

  Comparator #(.width(5)) comparator_1 (.a(rd_mem_wb), .b({5{1'b0}}), .eq(comparator_1_eq));  // open: gt, lt
  Comparator #(.width(5)) comparator_2 (.a(rt_id_ex), .b(rd_mem_wb), .eq(comparator_2_eq));  // open: gt, lt
  not not_1 (not_1_out, comparator_1_eq);
  Comparator #(.width(5)) comparator_3 (.a(rs_id_ex), .b(rd_ex_mem), .eq(comparator_3_eq));  // open: gt, lt
  Comparator #(.width(5)) comparator_4 (.a(rd_ex_mem), .b({5{1'b0}}), .eq(comparator_4_eq));  // open: gt, lt
  Comparator #(.width(5)) comparator_5 (.a(rt_id_ex), .b(rd_ex_mem), .eq(comparator_5_eq));  // open: gt, lt
  not not_2 (not_2_out, comparator_6_eq);
  Comparator #(.width(5)) comparator_6 (.a(rd_mem_wb), .b({5{1'b0}}), .eq(comparator_6_eq));  // open: gt, lt
  Comparator #(.width(5)) comparator_7 (.a(rs_id_ex), .b(rd_mem_wb), .eq(comparator_7_eq));  // open: gt, lt
  not not_3 (not_3_out, comparator_4_eq);
  and and_1 (ForwardA10, comparator_3_eq, not_3_out, RegWrite_ex_mem);
  and and_2 (ForwardB10, not_3_out, RegWrite_ex_mem, comparator_5_eq);
  and and_3 (ForwardB01, RegWrite_mem_wb, not_1_out, comparator_2_eq);
  and and_4 (ForwardA01, RegWrite_mem_wb, not_2_out, comparator_7_eq);
  // NOT_Gate not_4 is placed but not wired
  assign bit_extender_1_out = {{1{1'b0}}, ForwardA10};  // Bit_Extender bit_extender_1
  assign bit_extender_2_out = {{1{1'b0}}, ForwardB10};  // Bit_Extender bit_extender_2
  Shifter #(.width(2)) shifter_1 (.in(bit_extender_1_out), .\dist (1'b1), .out(shifter_1_out));
  Shifter #(.width(2)) shifter_2 (.in(bit_extender_2_out), .\dist (1'b1), .out(shifter_2_out));
  assign bit_extender_3_out = {{1{1'b0}}, ForwardA01};  // Bit_Extender bit_extender_3
  assign bit_extender_4_out = {{1{1'b0}}, ForwardB01};  // Bit_Extender bit_extender_4
  Adder #(.width(2)) adder_1 (.a(shifter_1_out), .b(bit_extender_3_out), .out(adder_1_out));  // open: cin, cout
  Adder #(.width(2)) adder_2 (.a(shifter_2_out), .b(bit_extender_4_out), .out(adder_2_out));  // open: cin, cout
  Multiplexer #(.select(2), .width(2)) multiplexer_1 (
    .in0(2'b00), .in1(2'b01), .in2(2'b10), .in3(2'b10), .out(ForwardA), .sel(adder_1_out));  // open: en
  Multiplexer #(.select(2), .width(2)) multiplexer_2 (
    .in0(2'b00), .in1(2'b01), .in2(2'b10), .in3(2'b10), .out(ForwardB), .sel(adder_2_out));  // open: en
  // NOT_Gate not_5 is placed but not wired

  // Notes on the sheet:
  //   ForwardB
  //   ForwardA
endmodule

module mem_wb (
  input  [4:0] WriteReg0,
  input  RegDst,
  input  MemToReg,
  input  RegWrite,
  input  [31:0] imm,
  input  [31:0] Result,
  input  [31:0] MemVal,
  input  [4:0] rd,
  input  lui,
  input  [31:0] instr,
  input  clk,
  output [4:0] WriteReg,
  output RegDst_2,
  output MemToReg_2,
  output RegWrite_2,
  output [31:0] imm_2,
  output [31:0] Result_2,
  output [31:0] MemVal_2,
  output [4:0] rd_2,
  output lui_2,
  output [31:0] instr_2
);

  Register #(.width(5)) register_1 (.D(WriteReg0), .Q(WriteReg), .clk(clk));  // open: en, clr
  Register #(.width(1)) register_2 (.D(RegDst), .Q(RegDst_2), .clk(clk));  // open: en, clr
  Register #(.width(1)) register_3 (.D(MemToReg), .Q(MemToReg_2), .clk(clk));  // open: en, clr
  Register #(.width(1)) register_4 (.D(RegWrite), .Q(RegWrite_2), .clk(clk));  // open: en, clr
  Register #(.width(32)) register_5 (.D(imm), .Q(imm_2), .clk(clk));  // open: en, clr
  Register #(.width(32)) register_6 (.D(Result), .Q(Result_2), .clk(clk));  // open: en, clr
  Register #(.width(32)) register_7 (.D(MemVal), .Q(MemVal_2), .clk(clk));  // open: en, clr
  Register #(.width(5)) register_8 (.D(rd), .Q(rd_2), .clk(clk));  // open: en, clr
  Register #(.width(1)) register_9 (.D(lui), .Q(lui_2), .clk(clk));  // open: en, clr
  Register #(.width(32)) register_10 (.D(instr), .Q(instr_2), .clk(clk));  // open: en, clr
endmodule

module AluSub (
  input  [23:0] PC,
  input  [31:0] rdValue,
  input  [31:0] imm,
  input  Lui,
  input  jl,
  output [31:0] wValue
);

  wire [31:0] adder_1_out, bit_extender_1_out, multiplexer_1_out, shifter_1_out;

  assign bit_extender_1_out = {{8{1'b0}}, PC};  // Bit_Extender bit_extender_1
  Shifter #(.width(32)) shifter_1 (.in(imm), .\dist (5'b10000), .out(shifter_1_out));
  Multiplexer #(.width(32)) multiplexer_1 (
    .in0(rdValue), .in1(shifter_1_out), .out(multiplexer_1_out), .sel(Lui));  // open: en
  Adder #(.width(32)) adder_1 (.a(bit_extender_1_out), .b(32'h2), .out(adder_1_out));  // open: cin, cout
  // Probe on wValue
  Multiplexer #(.width(32)) multiplexer_2 (
    .in0(multiplexer_1_out), .in1(adder_1_out), .out(wValue), .sel(jl));  // open: en

  // Other names for the same wires on the sheet: imm_mem_wb[31:0] = imm; Lui_mem_wb = Lui
endmodule

module HazDetectionUnit (
  input  MemRead,
  input  [4:0] rt_id_ex,
  input  [4:0] rt_if_id,
  input  [4:0] rs_if_id,
  output out
);

  wire comparator_1_eq, comparator_2_eq, or_1_out;

  Comparator #(.width(5)) comparator_1 (.a(rt_id_ex), .b(rt_if_id), .eq(comparator_1_eq));  // open: gt, lt
  Comparator #(.width(5)) comparator_2 (.a(rt_id_ex), .b(rs_if_id), .eq(comparator_2_eq));  // open: gt, lt
  or or_1 (or_1_out, comparator_1_eq, comparator_2_eq);
  and and_1 (out, MemRead, or_1_out);
endmodule

module HazardControl (
  input  RegDst0,
  input  AluSrc,
  input  MemToReg,
  input  RegWrite,
  input  MemRead,
  input  MemWrite,
  input  beq,
  input  bne,
  input  Lui,
  input  AluOp1,
  input  AluOp2,
  input  AluOp3,
  input  \byte ,
  input  u,
  input  j,
  input  jl,
  input  Stall,
  output RegDst,
  output AluSrc_2,
  output MemToReg_2,
  output RegWrite_2,
  output MemRead_2,
  output MemWrite_2,
  output beq_2,
  output bne_2,
  output Lui_2,
  output AluOp1_2,
  output AluOp2_2,
  output AluOp3_2,
  output byte_2,
  output u_2,
  output j_2,
  output jl_2
);

  Multiplexer multiplexer_1 (.in0(RegDst0), .in1(1'b0), .out(RegDst), .sel(Stall));  // open: en
  Multiplexer multiplexer_2 (.in0(AluSrc), .in1(1'b0), .out(AluSrc_2), .sel(Stall));  // open: en
  Multiplexer multiplexer_3 (.in0(MemToReg), .in1(1'b0), .out(MemToReg_2), .sel(Stall));  // open: en
  Multiplexer multiplexer_4 (.in0(RegWrite), .in1(1'b0), .out(RegWrite_2), .sel(Stall));  // open: en
  Multiplexer multiplexer_5 (.in0(MemRead), .in1(1'b0), .out(MemRead_2), .sel(Stall));  // open: en
  Multiplexer multiplexer_6 (.in0(MemWrite), .in1(1'b0), .out(MemWrite_2), .sel(Stall));  // open: en
  Multiplexer multiplexer_7 (.in0(beq), .in1(1'b0), .out(beq_2), .sel(Stall));  // open: en
  Multiplexer multiplexer_8 (.in0(bne), .in1(1'b0), .out(bne_2), .sel(Stall));  // open: en
  Multiplexer multiplexer_9 (.in0(Lui), .in1(1'b0), .out(Lui_2), .sel(Stall));  // open: en
  Multiplexer multiplexer_10 (.in0(AluOp1), .in1(1'b0), .out(AluOp1_2), .sel(Stall));  // open: en
  Multiplexer multiplexer_11 (.in0(AluOp2), .in1(1'b0), .out(AluOp2_2), .sel(Stall));  // open: en
  Multiplexer multiplexer_12 (.in0(AluOp3), .in1(1'b0), .out(AluOp3_2), .sel(Stall));  // open: en
  Multiplexer multiplexer_13 (.in0(\byte ), .in1(1'b0), .out(byte_2), .sel(Stall));  // open: en
  Multiplexer multiplexer_14 (.in0(u), .in1(1'b0), .out(u_2), .sel(Stall));  // open: en
  Multiplexer multiplexer_15 (.in0(j), .in1(1'b0), .out(j_2), .sel(Stall));  // open: en
  Multiplexer multiplexer_16 (.in0(jl), .in1(1'b0), .out(jl_2), .sel(Stall));  // open: en
endmodule
