// Logisim project mem.circ as structural Verilog: 1 circuit, main circuit main
module main (
  input  [31:0] Data_Mem_Addr,
  input  [31:0] Data_Mem_In,
  input  ACCESS_BYTE,
  input  MEM_WRITE,
  input  CLOCK,
  output [31:0] Data_Mem_Out
);

  wire [4:0] bpos5, bposx8;
  wire [23:0] addr, bpos, divider_1_out, faddr;
  wire [31:0] and_1_out, and_2_out, byteout, mask, multiplexer_2_out, ramout, shifter_2_out, shifter_3_out,
       subtractor_1_out, writebyte;

  Divider #(.width(24)) divider_1 (.a(addr), .b(24'h4), .out(divider_1_out), .rem(bpos));  // open: upper
  Bit_Extender #(.in_width(24), .out_width(5)) bit_extender_1 (.in(bpos), .out(bpos5));
  Multiplexer #(.width(24)) multiplexer_1 (
    .in0(addr), .in1(divider_1_out), .out(faddr), .sel(ACCESS_BYTE));  // open: en
  Shifter #(.width(5)) shifter_1 (.in(bpos5), .\dist (3'b011), .out(bposx8));
  Subtractor #(.width(32)) subtractor_1 (
    .a(Data_Mem_Addr), .b(32'h10010000), .out(subtractor_1_out));  // open: bin, bout
  Bit_Extender #(.in_width(32), .out_width(24)) bit_extender_2 (.in(subtractor_1_out), .out(addr));
  Multiplexer #(.width(32)) multiplexer_2 (
    .in0(Data_Mem_In), .in1(writebyte), .out(multiplexer_2_out), .sel(ACCESS_BYTE));  // open: en
  Shifter #(.width(32), .shift("lr")) shifter_2 (.in(ramout), .\dist (bposx8), .out(shifter_2_out));
  // Probe on ramout
  RAM #(.addrWidth(24), .dataWidth(32), .bus("separate")) ram_1 (
    .addr(faddr), .din(multiplexer_2_out), .data(ramout), .str(MEM_WRITE), .clk(CLOCK));  // open: sel, ld, clr
  assign and_1_out = Data_Mem_In & 32'hff;  // AND_Gate and_1, 32 bits wide
  Shifter #(.width(32)) shifter_3 (.in(and_1_out), .\dist (bposx8), .out(shifter_3_out));
  assign and_2_out = ramout & mask;  // AND_Gate and_2, 32 bits wide
  assign byteout = shifter_2_out & 32'hff;  // AND_Gate and_3, 32 bits wide
  Multiplexer #(.width(32)) multiplexer_3 (
    .in0(ramout), .in1(byteout), .out(Data_Mem_Out), .sel(ACCESS_BYTE));  // open: en
  // Probe on mask
  Shifter #(.width(32), .shift("rl")) shifter_4 (.in(32'hffffff00), .\dist (bposx8), .out(mask));
  assign writebyte = shifter_3_out | and_2_out;  // OR_Gate or_1, 32 bits wide

  // Other names for the same wires on the sheet: byte = ACCESS_BYTE; clk = CLOCK; memin[31:0] = Data_Mem_In

  // Notes on the sheet:
  //   These are INPUTS to the circuit
  //   These are INPUTS to the circuit
  //   DO NOT CHANGE THE LOCATIONS OF THE INPUTS/OUTPUTS! IF YOU DO SO, YOU NEED TO MAKE SURE THE PINS ARE AT THE RIGHT PLACE!
  //   Yet again, the clock is not an actual clock, but an input, one that will be driven from a higher circuit
  //   This is an OUTPUT to the circuit
endmodule
