// Logisim project reg_test.circ as structural Verilog: 1 circuit, main circuit main
module main (
);

  wire clock_1_out;
  wire [31:0] main_1_read_data_1, main_1_read_data_2, main_1_t0_value, main_1_t1_value, main_1_t2_value,
       main_1_t3_value;

  // Probe on main_1_t0_value
  // Probe on main_1_t1_value
  // Probe on main_1_t2_value
  // Probe on main_1_t3_value
  regfile_main main_1 (
    .Read_register_1(2'b01), .Read_register_2(2'b11), .write_register(2'b11), .write_data(32'h1234),
    .t0_Value(main_1_t0_value), .t1_Value(main_1_t1_value), .t2_Value(main_1_t2_value),
    .t3_Value(main_1_t3_value), .RegWrite(1'b1), .clock(clock_1_out), .Read_Data_1(main_1_read_data_1),
    .Read_Data_2(main_1_read_data_2));
  Clock clock_1 (.out(clock_1_out));
  // Probe on main_1_read_data_1
  // Probe on main_1_read_data_2
endmodule
