// Logisim project rotr.circ as structural Verilog: 7 circuits, main circuit main
module main (
  input  [15:0] in_1,
  input  [3:0] in_2
);

  wire clock_1_out;
  wire [15:0] rotr_1_out_3, shifter_1_out;

  rotr rotr_1 (.A(in_1), .B(in_2), .out_3(rotr_1_out_3));
  Register #(.width(16)) register_1 (.D(rotr_1_out_3), .clk(clock_1_out));  // open: en, Q, clr
  Clock clock_1 (.out(clock_1_out));
  Shifter #(.width(16), .shift("rr")) shifter_1 (.in(in_1), .\dist (in_2), .out(shifter_1_out));
  Register #(.width(16)) register_2 (.D(shifter_1_out), .clk(clock_1_out));  // open: en, Q, clr
endmodule

module Ex1 (
  input  [7:0] InputPin,
  output Out1,
  output [7:0] Out2
);

  wire [0:0] undriven;

  buf and_1 (Out1, undriven[0]);  // AND_Gate
endmodule

module rotr (
  input  [15:0] A,
  input  [3:0] B,
  output [15:0] out_3
);

  wire [15:0] a_b_1_out_3, a_b_2_out_3, bit_extender_1_out, bit_extender_2_out, subtractor_1_out;

  assign bit_extender_1_out = {{11{1'b0}}, 5'b10000};  // Bit_Extender bit_extender_1
  Subtractor #(.width(16)) subtractor_1 (
    .a(bit_extender_1_out), .b(bit_extender_2_out), .out(subtractor_1_out));  // open: bin, bout
  assign bit_extender_2_out = {{12{1'b0}}, B};  // Bit_Extender bit_extender_2
  A____B a_b_1 (.in_1(A), .in_2(B), .out_3(a_b_1_out_3));
  A____B_2 a_b_2 (.in_1(A), .in_2(subtractor_1_out[3:0]), .out_3(a_b_2_out_3));
  assign out_3 = a_b_2_out_3 | a_b_1_out_3;  // OR_Gate or_1, 16 bits wide
endmodule

module A___2 (
  input  [15:0] in_1,
  output [15:0] out_2
);

  wire [15:0] bit_extender_1_out;

  Divider #(.width(16)) divider_1 (.a(in_1), .b(bit_extender_1_out), .out(out_2));  // open: upper, rem
  assign bit_extender_1_out = {{14{1'b0}}, 2'b10};  // Bit_Extender bit_extender_1
endmodule

module A____B (
  input  [15:0] in_1,
  input  [3:0] in_2,
  output [15:0] out_3
);

  wire [15:0] a_2_1_out_2, a_2_2_out_2, a_2_3_out_2, a_2_4_out_2, a_2_5_out_2, a_2_6_out_2, a_2_7_out_2,
       a_2_8_out_2, a_2_9_out_2, a_2_10_out_2, a_2_11_out_2, a_2_12_out_2, a_2_13_out_2, a_2_14_out_2,
       a_2_15_out_2, a_2_16_out_2;

  A___2 a_2_1 (.in_1(in_1), .out_2(a_2_1_out_2));
  A___2 a_2_2 (.in_1(a_2_1_out_2), .out_2(a_2_2_out_2));
  A___2 a_2_3 (.in_1(a_2_4_out_2), .out_2(a_2_3_out_2));
  A___2 a_2_4 (.in_1(a_2_15_out_2), .out_2(a_2_4_out_2));
  A___2 a_2_5 (.in_1(a_2_2_out_2), .out_2(a_2_5_out_2));
  A___2 a_2_6 (.in_1(a_2_3_out_2), .out_2(a_2_6_out_2));
  A___2 a_2_7 (.in_1(a_2_5_out_2), .out_2(a_2_7_out_2));
  A___2 a_2_8 (.in_1(a_2_7_out_2), .out_2(a_2_8_out_2));
  A___2 a_2_9 (.in_1(a_2_6_out_2), .out_2(a_2_9_out_2));
  A___2 a_2_10 (.in_1(a_2_9_out_2), .out_2(a_2_10_out_2));
  A___2 a_2_11 (.in_1(a_2_8_out_2), .out_2(a_2_11_out_2));
  A___2 a_2_12 (.in_1(a_2_10_out_2), .out_2(a_2_12_out_2));
  A___2 a_2_13 (.in_1(a_2_11_out_2), .out_2(a_2_13_out_2));
  A___2 a_2_14 (.in_1(a_2_12_out_2), .out_2(a_2_14_out_2));
  A___2 a_2_15 (.in_1(a_2_13_out_2), .out_2(a_2_15_out_2));
  A___2 a_2_16 (.in_1(a_2_14_out_2), .out_2(a_2_16_out_2));
  Multiplexer #(.select(4), .width(16)) multiplexer_1 (
    .in0(in_1), .in1(a_2_1_out_2), .in2(a_2_2_out_2), .in3(a_2_5_out_2), .in4(a_2_7_out_2),
    .in5(a_2_8_out_2), .in6(a_2_11_out_2), .in7(a_2_13_out_2), .in8(a_2_4_out_2), .in9(a_2_3_out_2),
    .in10(a_2_6_out_2), .in11(a_2_9_out_2), .in12(a_2_10_out_2), .in13(a_2_12_out_2), .in14(a_2_14_out_2),
    .in15(a_2_16_out_2), .out(out_3), .sel(in_2), .en(1'b1));
endmodule

module A____B_2 (
  input  [15:0] in_1,
  input  [3:0] in_2,
  output [15:0] out_3
);

  wire [15:0] a_2_1_out_2, a_2_2_out_2, a_2_3_out_2, a_2_4_out_2, a_2_5_out_2, a_2_6_out_2, a_2_7_out_2,
       a_2_8_out_2, a_2_9_out_2, a_2_10_out_2, a_2_11_out_2, a_2_12_out_2, a_2_13_out_2, a_2_14_out_2,
       a_2_15_out_2, a_2_16_out_2;

  A___2_2 a_2_1 (.in_1(in_1), .out_2(a_2_1_out_2));
  A___2_2 a_2_2 (.in_1(a_2_15_out_2), .out_2(a_2_2_out_2));
  A___2_2 a_2_3 (.in_1(a_2_1_out_2), .out_2(a_2_3_out_2));
  A___2_2 a_2_4 (.in_1(a_2_2_out_2), .out_2(a_2_4_out_2));
  A___2_2 a_2_5 (.in_1(a_2_3_out_2), .out_2(a_2_5_out_2));
  A___2_2 a_2_6 (.in_1(a_2_4_out_2), .out_2(a_2_6_out_2));
  A___2_2 a_2_7 (.in_1(a_2_8_out_2), .out_2(a_2_7_out_2));
  A___2_2 a_2_8 (.in_1(a_2_5_out_2), .out_2(a_2_8_out_2));
  A___2_2 a_2_9 (.in_1(a_2_6_out_2), .out_2(a_2_9_out_2));
  A___2_2 a_2_10 (.in_1(a_2_9_out_2), .out_2(a_2_10_out_2));
  A___2_2 a_2_11 (.in_1(a_2_7_out_2), .out_2(a_2_11_out_2));
  A___2_2 a_2_12 (.in_1(a_2_10_out_2), .out_2(a_2_12_out_2));
  A___2_2 a_2_13 (.in_1(a_2_11_out_2), .out_2(a_2_13_out_2));
  A___2_2 a_2_14 (.in_1(a_2_12_out_2), .out_2(a_2_14_out_2));
  A___2_2 a_2_15 (.in_1(a_2_13_out_2), .out_2(a_2_15_out_2));
  A___2_2 a_2_16 (.in_1(a_2_14_out_2), .out_2(a_2_16_out_2));
  Multiplexer #(.select(4), .width(16)) multiplexer_1 (
    .in0(in_1), .in1(a_2_1_out_2), .in2(a_2_3_out_2), .in3(a_2_5_out_2), .in4(a_2_8_out_2),
    .in5(a_2_7_out_2), .in6(a_2_11_out_2), .in7(a_2_13_out_2), .in8(a_2_15_out_2), .in9(a_2_2_out_2),
    .in10(a_2_4_out_2), .in11(a_2_6_out_2), .in12(a_2_9_out_2), .in13(a_2_10_out_2), .in14(a_2_12_out_2),
    .in15(a_2_14_out_2), .out(out_3), .sel(in_2), .en(1'b1));
endmodule

module A___2_2 (
  input  [15:0] in_1,
  output [15:0] out_2
);

  wire [15:0] bit_extender_1_out;

  assign bit_extender_1_out = {{14{1'b0}}, 2'b10};  // Bit_Extender bit_extender_1
  Multiplier #(.width(16)) multiplier_1 (.a(in_1), .b(bit_extender_1_out), .out(out_2));  // open: cin, cout
endmodule
